# Fritzing sketch MaincontrollerWiring (saved by Fritzing 0.9.3b)

parts:
  Raspberry_Pi_1 = Raspberry Pi 3 [part_number=RPI-3-V1.2]
  Onderdeel1 = NRF24L01+ Breakout Board
  C1 = Capacitor Polarized [package=cpol-radial-100uf-25v]
  J1 = Piezo Speaker

nets:
  3V3: Raspberry_Pi_1.3v3, Onderdeel1.VCC, C1.+
  GND: Raspberry_Pi_1.GND, Onderdeel1.GND, Onderdeel1.CE, C1.-, J1.pin1
  N1: Raspberry_Pi_1.GPIO10, Onderdeel1.MOSI
  N2: Raspberry_Pi_1.GPIO9, Onderdeel1.MISO
  N3: Raspberry_Pi_1.GPIO11, Onderdeel1.SCK
  N4: Raspberry_Pi_1.GPIO21, J1.pin2
  N5: Raspberry_Pi_1.GPIO8, Onderdeel1.CS

notes:
  Configurationscreen
  (ribbon cable) ----------->>>>
