# Fritzing sketch SmartGridTableWiring (saved by Fritzing 0.9.3b)

parts:
  Onderdeel1 = RFID-RC522-v2
  Onderdeel2 = RFID-RC522-v2
  Onderdeel3 = RFID-RC522-v2
  Onderdeel4 = RFID-RC522-v2
  J1 = Screw terminal - 2 pins [package=THT]
  J2 = Screw terminal - 2 pins [package=THT]
  J3 = Screw terminal - 2 pins [package=THT]
  J4 = Screw terminal - 2 pins [package=THT]
  U1 = V_REG_LD1117VXX [package=78xxl]
  C1 = Electrolytic Capacitor [capacitance=1µF package="100 mil [THT, electrolytic]"]
  J5 = Power Jack [package=power_jack_smd]
  JP8 = Header 1 [package=1x01_offset]  # not connected
  JP9 = Header 1 [package=1x01_offset]  # not connected
  JP10 = Header 1 [package=1x01_offset]
  JP11 = Header 1 [package=1x01_offset]
  JP12 = Header 1 [package=1x01_offset]
  JP13 = Header 1 [package=1x01_offset]
  JP14 = Header 1 [package=1x01_offset]  # not connected
  JP15 = Header 1 [package=1x01_offset]
  JP16 = Header 1 [package=1x01_offset]
  JP17 = Header 1 [package=1x01_offset]
  JP18 = Header 1 [package=1x01_offset]
  JP19 = Header 1 [package=1x01_offset]
  JP20 = Header 1 [package=1x01_offset]
  JP21 = Header 1 [package=1x01_offset]
  JP22 = Header 1 [package=1x01_offset]
  JP23 = Header 1 [package=1x01_offset]
  JP24 = Header 1 [package=1x01_offset]
  JP25 = Header 1 [package=1x01_offset]
  JP26 = Header 1 [package=1x01_offset]
  JP27 = Header 1 [package=1x01_offset]  # not connected
  JP28 = Header 1 [package=1x01_offset]
  JP29 = Header 1 [package=1x01_offset]
  JP30 = Header 1 [package=1x01_offset]
  JP31 = Header 1 [package=1x01_offset]
  JP32 = Header 1 [package=1x01_offset]
  JP33 = Header 1 [package=1x01_offset]
  JP34 = Header 1 [package=1x01_offset]
  JP35 = Header 1 [package=1x01_offset]
  JP36 = Header 1 [package=1x01_offset]
  JP37 = Header 1 [package=1x01_offset]
  JP38 = Header 1 [package=1x01_offset]
  JP39 = Header 1 [package=1x01_offset]
  JP40 = Header 1 [package=1x01_offset]
  JP41 = Header 1 [package=1x01_offset]
  JP42 = Header 1 [package=1x01_offset]
  LPD8806_RGB_LED_Strip1 = LPD8806 RGB LED Strip
  JP45 = Header 1 [package=1x01_offset]
  JP46 = Header 1 [package=1x01_offset]
  JP47 = Header 1 [package=1x01_offset]
  JP48 = Header 1 [package=1x01_offset]
  JP49 = Header 1 [package=1x01_offset]
  JP50 = Header 1 [package=1x01_offset]
  JP51 = Header 1 [package=1x01_offset]
  JP52 = Header 1 [package=1x01_offset]
  JP53 = Header 1 [package=1x01_offset]
  JP54 = Header 1 [package=1x01_offset]
  JP55 = Header 1 [package=1x01_offset]
  JP56 = Header 1 [package=1x01_offset]
  JP57 = Header 1 [package=1x01_offset]
  JP59 = Header 1 [package=1x01_offset]
  JP60 = Header 1 [package=1x01_offset]
  JP61 = Header 1 [package=1x01_offset]
  JP62 = Header 1 [package=1x01_offset]
  JP63 = Header 1 [package=1x01_offset]
  JP64 = Header 1 [package=1x01_offset]
  JP65 = Header 1 [package=1x01_offset]
  JP66 = Header 1 [package=1x01_offset]
  JP67 = Header 1 [package=1x01_offset]
  JP68 = Header 1 [package=1x01_offset]
  JP69 = Header 1 [package=1x01_offset]
  JP70 = Header 1 [package=1x01_offset]
  JP71 = Header 1 [package=1x01_offset]
  JP72 = Header 1 [package=1x01_offset]
  JP73 = Header 1 [package=1x01_offset]
  JP74 = Header 1 [package=1x01_offset]
  JP75 = Header 1 [package=1x01_offset]
  JP76 = Header 1 [package=1x01_offset]
  JP77 = Header 1 [package=1x01_offset]
  Onderdeel6 = RFID-RC522-v2
  Onderdeel7 = RFID-RC522-v2
  Onderdeel8 = RFID-RC522-v2
  Onderdeel9 = RFID-RC522-v2
  J8 = Screw terminal - 2 pins [package=THT]
  J9 = Screw terminal - 2 pins [package=THT]
  Onderdeel10 = Arduino Nano (Rev3.0) (ICSP)
  Onderdeel11 = Arduino Nano (Rev3.0) (ICSP)
  LPD8806_RGB_LED_Strip2 = LPD8806 RGB LED Strip
  J10 = Screw terminal - 2 pins [package=THT]  # not connected
  J11 = Screw terminal - 2 pins [package=THT]  # not connected
  LPD8806_RGB_LED_Strip3 = LPD8806 RGB LED Strip
  LPD8806_RGB_LED_Strip4 = LPD8806 RGB LED Strip
  Onderdeel5 = NRF24L01
  JP79 = Header 1 [package=1x01_offset]
  JP80 = Header 1 [package=1x01_offset]
  C2 = Capacitor [package=cap-pth-small2]

nets:
  N1: Onderdeel1.SCK, JP20.1, JP24.1
  N2: Onderdeel1.MOSI, Onderdeel2.MOSI, Onderdeel3.MOSI, Onderdeel4.MOSI, JP29.1, JP35.1
  N3: Onderdeel1.MISO, Onderdeel2.MISO, Onderdeel3.MISO, Onderdeel4.MISO, JP30.1, JP36.1
  N4: Onderdeel1.IRQ, Onderdeel2.IRQ, Onderdeel3.IRQ, Onderdeel4.IRQ, JP31.1, JP37.1
  GND: Onderdeel1.GND, Onderdeel2.GND, Onderdeel3.GND, Onderdeel4.GND, JP32.1, JP38.1
  N5: Onderdeel1.RST, Onderdeel2.RST, Onderdeel3.RST, Onderdeel4.RST, JP33.1, JP39.1
  3.3V: Onderdeel1.3.3V, Onderdeel2.3.3V, Onderdeel3.3.3V, Onderdeel4.3.3V, JP34.1, JP40.1
  N6: Onderdeel2.SCK, JP21.1, JP25.1
  N7: Onderdeel3.SCK, JP22.1, JP26.1
  N8: Onderdeel4.SCK, JP23.1, JP28.1
  GND_2: J1.pin1, JP17.1, Onderdeel11.GND, Onderdeel5.GND
  N9: J1.pin2, Onderdeel11.VIN
  N10: J2.pin1, JP19.1, Onderdeel5.VCC
  N11: J3.pin1, U1.OUT, C1.+
  GND_3: J3.pin2, J4.pin1, U1.GND, C1.-, J5.GND, C2.2
  N12: J4.pin2, U1.IN, J5.PWR, C2.1
  N13: JP10.1, Onderdeel11.D5
  N14: JP11.1, Onderdeel11.D6
  N15: JP12.1, Onderdeel11.D7
  N16: JP13.1, Onderdeel11.D8
  N17: JP15.1, Onderdeel11.D11/MOSI, Onderdeel5.MOSI
  N18: JP16.1, Onderdeel11.D12/MISO, Onderdeel5.MISO
  N19: JP18.1, Onderdeel11.A0
  N20: JP41.1, LPD8806_RGB_LED_Strip1.CI, Onderdeel11.D2
  N21: JP42.1, LPD8806_RGB_LED_Strip1.DI, Onderdeel11.D3
  3.3V_2: JP45.1, JP51.1, Onderdeel6.3.3V, Onderdeel7.3.3V, Onderdeel8.3.3V, Onderdeel9.3.3V
  N22: JP46.1, JP52.1, Onderdeel6.RST, Onderdeel7.RST, Onderdeel8.RST, Onderdeel9.RST
  GND_4: JP47.1, JP53.1, Onderdeel6.GND, Onderdeel7.GND, Onderdeel8.GND, Onderdeel9.GND
  N23: JP48.1, JP54.1, Onderdeel6.IRQ, Onderdeel7.IRQ, Onderdeel8.IRQ, Onderdeel9.IRQ
  N24: JP49.1, JP55.1, Onderdeel6.MISO, Onderdeel7.MISO, Onderdeel8.MISO, Onderdeel9.MISO
  N25: JP50.1, JP56.1, Onderdeel6.MOSI, Onderdeel7.MOSI, Onderdeel8.MOSI, Onderdeel9.MOSI
  N26: JP57.1, JP62.1, Onderdeel6.SCK
  N27: JP59.1, JP63.1, Onderdeel7.SCK
  N28: JP60.1, JP64.1, Onderdeel8.SCK
  N29: JP61.1, JP65.1, Onderdeel9.SCK
  N30: JP66.1, J8.pin1
  N31: JP67.1, Onderdeel10.A0
  N32: JP68.1, J9.pin1, Onderdeel10.GND
  N33: JP69.1, Onderdeel10.D12/MISO
  N34: JP70.1, Onderdeel10.D10, Onderdeel10.D11/MOSI
  N35: JP71.1, Onderdeel10.3V3, Onderdeel10.D13/SCK
  N36: JP72.1, Onderdeel10.D8
  N37: JP73.1, Onderdeel10.D7
  N38: JP74.1, Onderdeel10.D6
  N39: JP75.1, Onderdeel10.D4, Onderdeel10.D5
  N40: JP76.1, Onderdeel10.A4
  N41: JP77.1, Onderdeel10.A5
  N42: J9.pin2, Onderdeel10.VIN
  N43: Onderdeel10.RESET, JP80.1
  N44: Onderdeel11.D9, Onderdeel5.CE
  N45: Onderdeel11.D10, Onderdeel5.CSN
  N46: Onderdeel11.A3, JP79.1
  N47: Onderdeel11.D13/SCK, Onderdeel5.SCK
  N48: LPD8806_RGB_LED_Strip2.DO, LPD8806_RGB_LED_Strip3.DI
  N49: LPD8806_RGB_LED_Strip2.CO, LPD8806_RGB_LED_Strip3.CI
  N50: LPD8806_RGB_LED_Strip3.DO, LPD8806_RGB_LED_Strip4.DI
  N51: LPD8806_RGB_LED_Strip3.CO, LPD8806_RGB_LED_Strip4.CI

notes:
  I2C conn
  SSN conn
  5V Power
  3.3V
  GND
  5V
  3,3V
  GND
  5V
  LED conn
  SPI conn / RESET conn
  BLACK RC522 !!!!
  Wiring shown;
  differs from BLUE version
  100 nF

custom parts:
  RFID-RC522-v2: A simple China made RFID-RC522 Reader; do check the pin labels, as this is a MFRC522 based clone.
  LPD8806 RGB LED Strip: Digitally addressable RGB LED strip
